# Fritzing sketch guirlande (saved by Fritzing 0.9.9b)
breadboards: 1

parts:
  Mod1 = Raspberry Pi Pico
  S1 = Pushbutton [package="[THT]"]
  HC-SR04_Sensor_1 = HC-SR04 Ultrasonic Distance Sensor
  R1 = Resistor [tolerance=±5% resistance=1k package="2512 [SMD]"]
  Q1 = NPN-Transistor [package="TO92 [THT]"]
  KY-1 = Keyes Relay [package=THT]

nets:
  N1: Mod1.pin_3, Mod1.pin_8, Mod1.pin_13, Mod1.pin_18, Mod1.pin_19, Mod1.pin_23, Mod1.pin_28, Mod1.pin_33, Mod1.pin_38, S1.Pin_1, S1.Pin_2, KY-1.ground
  N2: Mod1.pin_20, R1.Pin_0
  N3: Mod1.pin_21, KY-1.signal
  N4: Mod1.pin_22, Mod1.pin_40, HC-SR04_Sensor_1.VCC, HC-SR04_Sensor_1.TRIG
  N5: Mod1.pin_24, HC-SR04_Sensor_1.ECHO
  N6: Mod1.pin_39, KY-1.power
  N7: S1.Pin_3, S1.Pin_4
  N8: HC-SR04_Sensor_1.GND, Q1.B
  N9: R1.Pin_1, Q1.E

custom parts:
  Raspberry Pi Pico: Raspberry Pi Pico. Based around the RP2040 microcontroller the Pico is a low cost microcontroller device bringing Raspberry Pi quality, cost, and easy of use to the microcontroller space. Jan 2021, Split part in to two versions: tht (this one) and SMD. This one will drill holes for a .1 in header in pcb to allow plugging in the module as well as providing pads to solder the module to the top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
  Keyes Relay: The Keyes 5V relay module is suitable for SCM development, home appliance control. It uses a 5V~12V TIL control signal which can control DC / AC signal.
